# Fritzing sketch clock (saved by Fritzing 0.9.3b)
breadboards: 1

parts:
  T1 = TMP36 Temperature Sensor [package="TO92 [THT]"]
  U1 = atmega328 [package=dip]
  XTAL1 = Crystal [frequency="16 Mhz" package=THT]
  C1 = Ceramic Capacitor [capacitance=100nF package="100 mil [THT, multilayer]"]
  C2 = Ceramic Capacitor [capacitance=100nF package="100 mil [THT, multilayer]"]
  ZS-042_RTC1 = ZS-042 RTC Module
  Part2 = Seven-Segment LED Backpack 1.2 Inch Digits [part_number=1268]
  S1 = Pushbutton [package="[THT]"]
  Power_plug1 = Power plug
  U3 = Voltage Regulator - 3.3V [package="TO220 [THT]"]
  U2 = Voltage Regulator - 5V [package="TO220 [THT]"]

nets:
  N1: T1.+Vs, U1.AREF, U3.output_voltage
  N2: T1.Vout, U1.A0
  GND: T1.GND, U1.GND#21, ZS-042_RTC1.GND, Part2.GND, S1.Pin_1, S1.Pin_2, U3.GND
  N3: U1.D2, ZS-042_RTC1.SQW
  N4: U1.D3_(PWM), S1.Pin_3, S1.Pin_4
  VCC: U1.VCC, U1.AVCC, ZS-042_RTC1.VCC, Part2.VDD, Part2.VCCIO, U2.output_voltage
  GND_2: U1.GND#7, C1.1, C2.0, Power_plug1.GND, U2.GND
  N5: U1.XLAT1, XTAL1.pin_0, C1.0
  N6: U1.XLAT2, XTAL1.pin_1, C2.1
  N7: U1.A4, ZS-042_RTC1.SDA, Part2.SDA
  N8: U1.A5, ZS-042_RTC1.SCL, Part2.SCL
  N9: Power_plug1.VCC, U3.input_voltage, U2.input_voltage

custom parts:
  Seven-Segment LED Backpack 1.2 Inch Digits: This jumbo 1.2" 7-segment LED display includes a driver chip for simple control via an I2C interface. The backpack features address-selection jumpers so you can connect up to eight displays on a single I2C bus.
