# Fritzing sketch LED Driver (saved by Fritzing 0.9.3b)
breadboards: 1

parts:
  Q1 = Basic FET N-Channel [package="TO220 [THT]"]
  Q2 = Basic FET N-Channel [package="TO220 [THT]"]
  Power_plug1 = Power plug
  Q3 = Basic FET N-Channel [package="TO220 [THT]"]
  R1 = Resistor [tolerance=±5% resistance=10k package=THT]
  R2 = Resistor [tolerance=±5% resistance=10k package=THT]
  R3 = Resistor [tolerance=±5% resistance=10k package=THT]
  Raspberry_Pi1 = Raspberry Pi 2
  LED1 = RGB LED (com. cathode, rgb) [package="5 mm [THT]"]

nets:
  N1: Q1.gate, R3.Pin_1, Raspberry_Pi1.GPIO4, Raspberry_Pi1.GPIO14
  N2: Q1.drain, LED1.blue_anode
  GND: Q1.source, Q2.source, Power_plug1.GND, Q3.source, R1.Pin_0, R2.Pin_0, R3.Pin_0, Raspberry_Pi1.GND
  N3: Q2.gate, R2.Pin_1, Raspberry_Pi1.GPIO3
  N4: Q2.drain, LED1.green_anode
  N5: Power_plug1.VCC, LED1.common_cathode
  N6: Q3.gate, R1.Pin_1, Raspberry_Pi1.GPIO2, Raspberry_Pi1.5V
  N7: Q3.drain, LED1.red_anode
